# Fritzing sketch schematic (saved by Fritzing 0.9.3b)

parts:
  U1 = ESP32S-HiLetgo [part_number=ESP32S-HiLetgo]
  U2 = NodeMCU V3.0
  DHT11_1 = DHT11 module
  TFT1 = 1.8" TFT Display with uSD
  DS1 = DS18B20 1-Wire Temperature Sensor Probe Cable
  S3 = Tilt Switch [package=THT]
  S2 = Tilt Switch [package=THT]
  S4 = Tilt Switch [package=THT]
  S5 = Tilt Switch [package=THT]
  R1 = Resistor [tolerance=±5% resistance=470k package=THT]

nets:
  N1: U1.3.3, TFT1.MISO
  N2: U1.GPIO14, S5.Pin_2
  GND: U1.GND, DHT11_1.GND, TFT1.BL, S3.Pin_2, S2.Pin_2, S4.Pin_1, S5.Pin_1
  N3: U1.GPIO13, DHT11_1.DATA
  VIN: U1.VIN, DHT11_1.VCC
  N4: U1.GPIO2, TFT1.MOSI
  N5: U1.GPIO4, TFT1.SCK
  N6: U1.GPIO5, TFT1.SDCS
  N7: U1.GPIO18, TFT1.RST
  N8: U1.GPIO19, S4.Pin_2
  N9: U1.GPIO21, S3.Pin_1
  N10: U1.GPIO22, S2.Pin_1
  N11: U1.GPIO23, TFT1.D/C
  N12: U2.D2, DS1.DQ, R1.Pin_0
  3V3: U2.3V3, DS1.VDD, R1.Pin_1
  GND_2: U2.GND, DS1.GND, DS1.shield

custom parts:
  ESP32S-HiLetgo: HiLetgo ESP-WROOM-32 ESP32 ESP-32S Development Board 2.4GHz Dual-Mode WiFi + Bluetooth Dual Cores Microcontroller The ESP32 integrated with Antenna switches, RF Balun, power amplifiers, low-noise amplifiers, filters, and management modules, and the entire solution occupies the least area of PCB. 2.4 GHz Wi-Fi plus Bluetooth dual-mode chip, with TSMC Ultra-low power consumption 40nm technology,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
  NodeMCU V3.0: ESP8266 based NodeMCU
  DHT11 module: DHT11 black pcb module
  1.8" TFT Display with uSD: 1.8" TFT Display with SPI control and MicroSD card
